// Logisim project GangeMedTi.circ as structural Verilog: 3 circuits, main circuit Half Adder
module Half_Adder (
  input  X_inn,
  input  Y_inn,
  output Sum,
  output Cout
);

  and and_1 (Cout, X_inn, Y_inn);
  xor xor_1 (Sum, X_inn, Y_inn);
endmodule

module Full_Adder (
  input  X_inn,
  input  Y_inn,
  input  C_inn,
  output Sum,
  output Cout
);

  wire and_1_out, and_2_out, and_3_out, xor_1_out;

  xor xor_1 (xor_1_out, X_inn, Y_inn);
  and and_1 (and_1_out, X_inn, Y_inn);
  and and_2 (and_2_out, X_inn, C_inn);
  and and_3 (and_3_out, C_inn, Y_inn);
  xor xor_2 (Sum, xor_1_out, C_inn);
  or or_1 (Cout, and_1_out, and_2_out, and_3_out);
endmodule

module mul10 (
  input  in_1,
  input  in_2,
  input  in_3,
  input  in_4,
  input  in_5,
  output out_6,
  output out_7,
  output out_8,
  output out_9,
  output out_10,
  output out_11,
  output out_12,
  output out_13,
  output out_14
);

  wire full_adder_1_cout, full_adder_1_sum, full_adder_2_cout, full_adder_2_sum, full_adder_3_cout,
       full_adder_3_sum, full_adder_4_cout, full_adder_4_sum, full_adder_5_cout, full_adder_5_sum,
       full_adder_6_cout, full_adder_6_sum, full_adder_7_cout, full_adder_7_sum, full_adder_8_cout,
       full_adder_8_sum, full_adder_9_cout, full_adder_9_sum, full_adder_10_cout, full_adder_10_sum,
       full_adder_11_cout, full_adder_11_sum, full_adder_12_cout, full_adder_12_sum, full_adder_13_cout,
       full_adder_13_sum, full_adder_14_cout, full_adder_14_sum, full_adder_15_cout, full_adder_15_sum,
       full_adder_16_cout, full_adder_16_sum, half_adder_2_cout, half_adder_3_cout, half_adder_3_sum,
       half_adder_4_cout, half_adder_5_cout, half_adder_5_sum, half_adder_6_cout, half_adder_7_cout,
       half_adder_8_cout, half_adder_9_cout, half_adder_10_cout, half_adder_11_cout, half_adder_11_sum,
       half_adder_12_cout, half_adder_12_sum, half_adder_13_cout, half_adder_13_sum, half_adder_14_cout,
       half_adder_14_sum, xor_1_out, xor_2_out, xor_3_out, xor_4_out, xor_5_out, xor_6_out, xor_7_out,
       xor_8_out;

  xor xor_1 (xor_1_out, in_1, half_adder_3_cout);
  Half_Adder half_adder_1 (.Sum(out_7), .X_inn(xor_1_out), .Y_inn(half_adder_2_cout));  // open: Cout
  xor xor_2 (xor_2_out, in_1, half_adder_3_sum);
  Half_Adder half_adder_2 (.Cout(half_adder_2_cout), .Sum(out_8), .X_inn(xor_2_out), .Y_inn(half_adder_4_cout));
  Half_Adder half_adder_3 (
    .Cout(half_adder_3_cout), .Sum(half_adder_3_sum), .X_inn(full_adder_1_cout), .Y_inn(half_adder_5_cout));
  xor xor_3 (xor_3_out, in_1, half_adder_5_sum);
  Half_Adder half_adder_4 (.Cout(half_adder_4_cout), .Sum(out_9), .X_inn(xor_3_out), .Y_inn(half_adder_6_cout));
  Full_Adder full_adder_1 (
    .Cout(full_adder_1_cout), .Sum(full_adder_1_sum), .X_inn(full_adder_2_cout), .Y_inn(full_adder_2_cout),
    .C_inn(full_adder_3_cout));
  Half_Adder half_adder_5 (
    .Cout(half_adder_5_cout), .Sum(half_adder_5_sum), .X_inn(full_adder_1_sum), .Y_inn(full_adder_4_cout));
  xor xor_4 (xor_4_out, in_1, full_adder_4_sum);
  Half_Adder half_adder_6 (.Cout(half_adder_6_cout), .Sum(out_10), .X_inn(xor_4_out), .Y_inn(half_adder_7_cout));
  Full_Adder full_adder_2 (
    .Cout(full_adder_2_cout), .Sum(full_adder_2_sum), .X_inn(full_adder_8_cout), .Y_inn(full_adder_8_cout),
    .C_inn(full_adder_5_cout));
  Full_Adder full_adder_3 (
    .Cout(full_adder_3_cout), .Sum(full_adder_3_sum), .X_inn(full_adder_2_sum), .Y_inn(full_adder_2_sum),
    .C_inn(full_adder_6_cout));
  Full_Adder full_adder_4 (
    .Cout(full_adder_4_cout), .Sum(full_adder_4_sum), .X_inn(full_adder_3_sum), .Y_inn(full_adder_8_cout),
    .C_inn(full_adder_7_cout));
  xor xor_5 (xor_5_out, in_1, full_adder_7_sum);
  Half_Adder half_adder_7 (.Cout(half_adder_7_cout), .Sum(out_11), .X_inn(xor_5_out), .Y_inn(half_adder_8_cout));
  Full_Adder full_adder_5 (
    .Cout(full_adder_5_cout), .Sum(full_adder_5_sum), .X_inn(full_adder_8_sum), .Y_inn(full_adder_8_sum),
    .C_inn(full_adder_9_cout));
  Full_Adder full_adder_6 (
    .Cout(full_adder_6_cout), .Sum(full_adder_6_sum), .X_inn(full_adder_5_sum), .Y_inn(full_adder_5_sum),
    .C_inn(full_adder_10_cout));
  Full_Adder full_adder_7 (
    .Cout(full_adder_7_cout), .Sum(full_adder_7_sum), .X_inn(full_adder_6_sum), .Y_inn(full_adder_8_sum),
    .C_inn(full_adder_11_cout));
  xor xor_6 (xor_6_out, in_1, full_adder_11_sum);
  Half_Adder half_adder_8 (.Cout(half_adder_8_cout), .Sum(out_12), .X_inn(xor_6_out), .Y_inn(half_adder_9_cout));
  Full_Adder full_adder_8 (
    .Cout(full_adder_8_cout), .Sum(full_adder_8_sum), .X_inn(in_2), .Y_inn(in_2), .C_inn(full_adder_12_cout));
  Full_Adder full_adder_9 (
    .Cout(full_adder_9_cout), .Sum(full_adder_9_sum), .X_inn(full_adder_12_sum), .Y_inn(full_adder_12_sum),
    .C_inn(full_adder_13_cout));
  Full_Adder full_adder_10 (
    .Cout(full_adder_10_cout), .Sum(full_adder_10_sum), .X_inn(full_adder_9_sum), .Y_inn(full_adder_9_sum),
    .C_inn(full_adder_14_cout));
  Full_Adder full_adder_11 (
    .Cout(full_adder_11_cout), .Sum(full_adder_11_sum), .X_inn(full_adder_10_sum), .Y_inn(full_adder_12_sum),
    .C_inn(full_adder_15_cout));
  xor xor_7 (xor_7_out, in_1, full_adder_15_sum);
  Half_Adder half_adder_9 (.Cout(half_adder_9_cout), .Sum(out_13), .X_inn(xor_7_out), .Y_inn(half_adder_10_cout));
  Full_Adder full_adder_12 (
    .Cout(full_adder_12_cout), .Sum(full_adder_12_sum), .X_inn(in_3), .Y_inn(in_3), .C_inn(full_adder_16_cout));
  Full_Adder full_adder_13 (
    .Cout(full_adder_13_cout), .Sum(full_adder_13_sum), .X_inn(full_adder_16_sum), .Y_inn(full_adder_16_sum),
    .C_inn(half_adder_11_cout));
  Full_Adder full_adder_14 (
    .Cout(full_adder_14_cout), .Sum(full_adder_14_sum), .X_inn(full_adder_13_sum), .Y_inn(full_adder_13_sum),
    .C_inn(half_adder_12_cout));
  Full_Adder full_adder_15 (
    .Cout(full_adder_15_cout), .Sum(full_adder_15_sum), .X_inn(full_adder_14_sum), .Y_inn(full_adder_16_sum),
    .C_inn(half_adder_13_cout));
  xor xor_8 (xor_8_out, in_1, half_adder_13_sum);
  Half_Adder half_adder_10 (.Cout(half_adder_10_cout), .Sum(out_14), .X_inn(xor_8_out), .Y_inn(in_1));
  Full_Adder full_adder_16 (
    .Cout(full_adder_16_cout), .Sum(full_adder_16_sum), .X_inn(in_4), .Y_inn(in_4), .C_inn(half_adder_14_cout));
  Half_Adder half_adder_11 (
    .Cout(half_adder_11_cout), .Sum(half_adder_11_sum), .X_inn(half_adder_14_sum), .Y_inn(half_adder_14_sum));
  Half_Adder half_adder_12 (
    .Cout(half_adder_12_cout), .Sum(half_adder_12_sum), .X_inn(half_adder_11_sum), .Y_inn(half_adder_11_sum));
  Half_Adder half_adder_13 (
    .Cout(half_adder_13_cout), .Sum(half_adder_13_sum), .X_inn(half_adder_12_sum), .Y_inn(half_adder_14_sum));
  Half_Adder half_adder_14 (.Cout(half_adder_14_cout), .Sum(half_adder_14_sum), .X_inn(in_5), .Y_inn(in_5));

  assign out_6 = in_1;
endmodule
