// Logisim project Oblig2.circ as structural Verilog: 6 circuits, main circuit main
module main (
  input  in_1
);

  wire clock_1_out, decoder_1_out8, decoder_1_out9, decoder_1_out10, decoder_1_out11, not_1_out, not_2_out,
       not_3_out, or_1_out, or_2_out, or_3_out, R_out;
  wire [3:0] counter_1_out;
  wire [7:0] controlled_buffer_1_out, overwrite_lsb_msb_1_output, R_2_q, ram_1_data, ram_2_data;

  Clock clock_1 (.out(clock_1_out));
  Button R (.out(R_out));
  not not_1 (not_1_out, clock_1_out);
  Counter counter_1 (.Clock(clock_1_out), .Reset(R_out), .Out(counter_1_out));
  RAM #(.addrWidth(4), .bus("asynch")) ram_1 (
    .addr(counter_1_out), .data(ram_1_data), .sel(in_1), .ld(1'b1), .clr(1'b0));
  Decoder #(.select(4), .enable("false")) decoder_1 (
    .out8(decoder_1_out8), .out9(decoder_1_out9), .out10(decoder_1_out10), .out11(decoder_1_out11),
    .sel(ram_1_data[7:4]));  // open: out0, out1, out2, out3, out4, out5, out6, out7, out12, out13, out14, out15
  or or_1 (or_1_out, not_2_out, decoder_1_out9);
  or or_2 (or_2_out, decoder_1_out8, decoder_1_out9);
  not not_2 (not_2_out, decoder_1_out8);
  Overwrite_LSB_MSB overwrite_lsb_msb_1 (
    .Initial_value(R_2_q), .bits_to_overwrite_LSB_MSB(ram_1_data[3:0]),
    .Overwrite__LSB_when_0__MSB_when_1(or_1_out), .Output(overwrite_lsb_msb_1_output));
  assign controlled_buffer_1_out = or_2_out ? overwrite_lsb_msb_1_output : 8'bz;  // Controlled_Buffer controlled_buffer_1
  assign controlled_buffer_1_out = decoder_1_out10 ? ram_2_data : 8'bz;  // Controlled_Buffer controlled_buffer_2
  RAM #(.addrWidth(4), .bus("asynch")) ram_2 (
    .addr(ram_1_data[3:0]), .data(ram_2_data), .sel(not_1_out), .ld(or_3_out), .clr(1'b0));
  or or_3 (or_3_out, decoder_1_out10, not_3_out);
  not not_3 (not_3_out, decoder_1_out11);
  Register #(.trigger("falling")) R_2 (
    .D(controlled_buffer_1_out), .en(or_2_out), .Q(R_2_q), .clk(clock_1_out));  // open: clr
  assign ram_2_data = decoder_1_out11 ? R_2_q : 8'bz;  // Controlled_Buffer controlled_buffer_3
endmodule

// Count
module Counter (
  input  Clock,
  input  Reset,
  output [3:0] Out
);

  wire adder_1_cout, not_1_out;
  wire [3:0] adder_1_out;

  not not_1 (not_1_out, adder_1_cout);
  Register #(.width(4)) register_1 (.D(adder_1_out), .en(not_1_out), .Q(Out), .clk(Clock), .clr(Reset));
  Adder #(.width(4)) adder_1 (.a(Out), .b(4'b0001), .out(adder_1_out), .cout(adder_1_cout));  // open: cin
endmodule

module MUX (
  input  [3:0] Data_Adresse,
  input  [3:0] Instruksjon,
  output [3:0] Load_LSB_med_dette,
  output [3:0] Load_MSB_med_dette,
  output [3:0] Load_R_fra_denne_adressen,
  output [3:0] Write_R_til_denne_adressen
);

  wire and_1_out, and_2_out, and_3_out, and_4_out, and_5_out, and_6_out, and_7_out, and_8_out, and_9_out,
       not_1_out, not_2_out, not_3_out, not_4_out, not_5_out;

  not not_1 (not_1_out, Instruksjon[1]);
  not not_2 (not_2_out, Instruksjon[2]);
  and and_1 (and_1_out, Instruksjon[3], not_2_out);
  assign Load_LSB_med_dette = and_2_out ? Data_Adresse : 4'bz;  // Controlled_Buffer controlled_buffer_1
  and and_2 (and_2_out, and_4_out, and_1_out);
  and and_3 (and_3_out, and_5_out, and_1_out);
  and and_4 (and_4_out, not_1_out, not_3_out);
  and and_5 (and_5_out, not_4_out, Instruksjon[0]);
  not not_3 (not_3_out, Instruksjon[0]);
  not not_4 (not_4_out, Instruksjon[1]);
  assign Load_MSB_med_dette = and_3_out ? Data_Adresse : 4'bz;  // Controlled_Buffer controlled_buffer_2
  assign Load_R_fra_denne_adressen = and_6_out ? Data_Adresse : 4'bz;  // Controlled_Buffer controlled_buffer_3
  and and_6 (and_6_out, and_7_out, and_1_out);
  and and_7 (and_7_out, Instruksjon[1], not_5_out);
  not not_5 (not_5_out, Instruksjon[0]);
  assign Write_R_til_denne_adressen = and_8_out ? Data_Adresse : 4'bz;  // Controlled_Buffer controlled_buffer_4
  and and_8 (and_8_out, and_9_out, and_1_out);
  and and_9 (and_9_out, Instruksjon[1], Instruksjon[0]);
endmodule

module _4_bit_Tri_state_Buffer (
  input  Enable_1,
  input  [3:0] Inn_1,
  input  [3:0] Inn_2,
  input  Enable_2,
  output [3:0] Out_1,
  output [3:0] Out_2
);

  wire clock_1_out;
  wire [3:0] register_1_q, register_2_q;

  Register #(.width(4)) register_1 (.D(Inn_1), .Q(register_1_q), .clk(clock_1_out));  // open: en, clr
  Register #(.width(4)) register_2 (.D(Inn_2), .Q(register_2_q), .clk(clock_1_out));  // open: en, clr
  Clock clock_1 (.out(clock_1_out));
  assign Out_1 = Enable_1 ? register_1_q : 4'bz;  // Controlled_Buffer controlled_buffer_1
  assign Out_2 = Enable_2 ? register_2_q : 4'bz;  // Controlled_Buffer controlled_buffer_2
endmodule

// OW
module Overwrite_LSB_MSB (
  input  [7:0] Initial_value,
  input  [3:0] bits_to_overwrite_LSB_MSB,
  input  Overwrite__LSB_when_0__MSB_when_1,
  output [7:0] Output
);

  wire not_1_out, not_2_out;

  assign Output[7:4] = Overwrite__LSB_when_0__MSB_when_1 ? bits_to_overwrite_LSB_MSB : 4'bz;  // Controlled_Buffer controlled_buffer_1
  not not_1 (not_1_out, Overwrite__LSB_when_0__MSB_when_1);
  not not_2 (not_2_out, Overwrite__LSB_when_0__MSB_when_1);
  assign Output[3:0] = Overwrite__LSB_when_0__MSB_when_1 ? Initial_value[3:0] : 4'bz;  // Controlled_Buffer controlled_buffer_2
  assign Output[7:4] = not_2_out ? Initial_value[7:4] : 4'bz;  // Controlled_Buffer controlled_buffer_3
  assign Output[3:0] = not_1_out ? bits_to_overwrite_LSB_MSB : 4'bz;  // Controlled_Buffer controlled_buffer_4
endmodule

module Eksempel (
  input  [7:0] in_1,
  input  [7:0] in_2,
  input  [7:0] in_3,
  input  in_4,
  input  in_5,
  input  in_6,
  output [7:0] out_7,
  output [7:0] out_8,
  output [7:0] out_9
);

  assign out_7 = in_4 ? in_1 : 8'bz;  // Controlled_Buffer controlled_buffer_1
  assign out_7 = in_5 ? in_2 : 8'bz;  // Controlled_Buffer controlled_buffer_2
  assign out_7 = in_6 ? in_3 : 8'bz;  // Controlled_Buffer controlled_buffer_3

  assign out_8 = out_7;
  assign out_9 = out_7;

  // Notes on the sheet:
  //   Dataminne utgang
  //   Register inngang
  //   Register utgang
endmodule
