// Logisim project Oppgave1.circ as structural Verilog
module Counter (
  output [3:0] out_1
);

  wire adder_1_cout, clock_1_out, not_1_out;
  wire [3:0] adder_1_out;

  not not_1 (not_1_out, adder_1_cout);
  Clock clock_1 (.out(clock_1_out));
  Register #(.width(4)) register_1 (.D(adder_1_out), .en(not_1_out), .Q(out_1), .clk(clock_1_out), .clr(1'b0));
  Adder #(.width(4)) adder_1 (.a(out_1), .b(4'b0001), .out(adder_1_out), .cin(1'b0), .cout(adder_1_cout));
endmodule

module StopAt15 (
);

  wire undriven;

  Counter counter_1 ();  // open: out_1
  // Probe on undriven
endmodule
