// Logisim project Oppgave2.circ as structural Verilog
module Tristate (
  input  Enable_1,
  input  [3:0] Inn_1,
  input  [3:0] Inn_2,
  input  Enable_2,
  output [3:0] Out_1,
  output [3:0] Out_2
);

  wire clock_1_out;
  wire [3:0] register_1_q, register_2_q;

  Register #(.width(4)) register_1 (.D(Inn_1), .Q(register_1_q), .clk(clock_1_out));  // open: en, clr
  Register #(.width(4)) register_2 (.D(Inn_2), .Q(register_2_q), .clk(clock_1_out));  // open: en, clr
  Clock clock_1 (.out(clock_1_out));
  assign Out_1 = Enable_1 ? register_1_q : 4'bz;  // Controlled_Buffer controlled_buffer_1
  assign Out_2 = Enable_2 ? register_2_q : 4'bz;  // Controlled_Buffer controlled_buffer_2
endmodule

module MUX (
  input  [3:0] Inn_1,
  input  [3:0] Inn_2,
  input  Select,
  output [3:0] out_4
);

  wire not_1_out, not_2_out;
  wire [3:0] tristate_1_out_1, tristate_1_out_2;

  Tristate tristate_1 (
    .Inn_1(Inn_1), .Inn_2(Inn_2), .Enable_1(Select), .Enable_2(not_1_out), .Out_1(tristate_1_out_1),
    .Out_2(tristate_1_out_2));
  not not_1 (not_1_out, Select);
  not not_2 (not_2_out, Select);
  assign out_4 = Select ? tristate_1_out_1 : 4'bz;  // Controlled_Buffer controlled_buffer_1
  assign out_4 = not_2_out ? tristate_1_out_2 : 4'bz;  // Controlled_Buffer controlled_buffer_2
endmodule
